// Logisim project CT8.circ as structural Verilog: 18 circuits, main circuit main
module main (
);

  CPU cpu_1 ();
endmodule

module ALU (
  input  CEnbl,
  input  Cin,
  input  OutEn,
  input  [7:0] A,
  input  [7:0] B,
  input  [5:0] in_6,
  output SF,
  output [7:0] Dout,
  output COut
);

  wire and_1_out, or_2_out, xor_2_out;
  wire [7:0] adder_1_out, and_2_out, controlled_buffer_1_out, not_1_out, or_1_out, xor_1_out, xor_3_out;

  // Probe on A
  // Probe on B
  assign xor_1_out = B ^ {8{in_6[1]}};  // XOR_Gate xor_1, 8 bits wide
  and and_1 (and_1_out, CEnbl, Cin);
  xor xor_2 (xor_2_out, and_1_out, in_6[1]);
  Adder adder_1 (.a(A), .b(xor_1_out), .out(adder_1_out), .cin(xor_2_out), .cout(COut));
  assign and_2_out = A & xor_1_out;  // AND_Gate and_2, 8 bits wide
  assign or_1_out = A | xor_1_out;  // OR_Gate or_1, 8 bits wide
  assign xor_3_out = A ^ xor_1_out;  // XOR_Gate xor_3, 8 bits wide
  assign not_1_out = ~xor_1_out;  // NOT_Gate not_1, 8 bits wide
  or or_2 (or_2_out, in_6[1], in_6[0]);
  assign controlled_buffer_1_out = or_2_out ? adder_1_out : 8'bz;  // Controlled_Buffer controlled_buffer_1
  assign controlled_buffer_1_out = in_6[2] ? and_2_out : 8'bz;  // Controlled_Buffer controlled_buffer_2
  assign controlled_buffer_1_out = in_6[3] ? or_1_out : 8'bz;  // Controlled_Buffer controlled_buffer_3
  assign controlled_buffer_1_out = in_6[4] ? xor_3_out : 8'bz;  // Controlled_Buffer controlled_buffer_4
  assign controlled_buffer_1_out = in_6[5] ? not_1_out : 8'bz;  // Controlled_Buffer controlled_buffer_5
  // Probe on Dout
  assign Dout = OutEn ? controlled_buffer_1_out : 8'bz;  // Controlled_Buffer controlled_buffer_6

  assign SF = OutEn;
endmodule

module instrDecoder (
  input  [7:0] instr,
  output ADD_op,
  output HLT,
  output SUB_op,
  output AND_op,
  output CMP_op,
  output OR_op,
  output ALUop,
  output XOR_op,
  output NOT_op,
  output LW,
  output SW,
  output MOV,
  output LDA,
  output JNZ,
  output JZ,
  output JMP,
  output HLuse,
  output [2:0] REG_MUX,
  output immReg,
  output NOP
);

  wire and_3_out, and_7_out, demultiplexer_1_out3, demultiplexer_1_out4, demultiplexer_1_out7,
       demultiplexer_2_out1, imm, NOP_t, nor_1_out, or_3_out;

  and and_1 (HLT, instr[0], instr[1], instr[2], instr[3]);
  and and_2 (ALUop, ~HLT, instr[3]);  // AND_Gate
  nor nor_1 (nor_1_out, HLT, instr[3]);
  Demultiplexer #(.select(3)) demultiplexer_1 (
    .out1(LW), .out2(SW), .out3(demultiplexer_1_out3), .out4(demultiplexer_1_out4), .out5(JNZ), .out6(JZ),
    .out7(demultiplexer_1_out7), .in(nor_1_out), .sel(instr[2:0]));  // open: out0
  and and_3 (and_3_out, ~instr[0], ~instr[1], ~instr[2], ~instr[3]);  // AND_Gate
  Demultiplexer #(.select(3)) demultiplexer_2 (
    .out0(ADD_op), .out1(demultiplexer_2_out1), .out2(AND_op), .out3(OR_op), .out4(XOR_op), .out5(NOT_op),
    .out6(CMP_op), .in(ALUop), .sel(instr[2:0]));  // open: out7
  and and_4 (NOP_t, demultiplexer_1_out3, imm);
  and and_5 (LDA, imm, demultiplexer_1_out4);
  not not_1 (imm, instr[4]);
  or or_1 (NOP, NOP_t, and_3_out);
  and and_6 (MOV, demultiplexer_1_out3, ~imm);  // AND_Gate
  and and_7 (and_7_out, ~LDA, demultiplexer_1_out4);  // AND_Gate
  or or_2 (JMP, and_7_out, demultiplexer_1_out7);
  or or_3 (or_3_out, JNZ, JZ, JMP, LW, SW);
  or or_4 (SUB_op, demultiplexer_2_out1, CMP_op);
  and and_8 (HLuse, or_3_out, instr[4]);

  assign immReg = instr[4];
  assign REG_MUX = instr[7:5];

  // Notes on the sheet:
  //   0= imm 1= reg op
  //   regImportant
  //   NoREG
endmodule

module regs (
  input  [7:0] Din,
  input  WE,
  input  Clck,
  input  Rst,
  input  OE,
  output [7:0] Dout,
  output [7:0] alwaysDOUT
);

  Register register_1 (.D(Din), .en(WE), .clk(Clck), .Q(alwaysDOUT), .clr(Rst));
  assign Dout = OE ? alwaysDOUT : 8'bz;  // Controlled_Buffer controlled_buffer_1
endmodule

module instrReg (
  input  [7:0] instIn,
  input  WE,
  input  Clck,
  input  Rst,
  output [7:0] out_5
);

  Register register_1 (.D(instIn), .en(WE), .clk(Clck), .Q(out_5), .clr(Rst));
endmodule

module PC (
  input  load,
  input  [15:0] AddrBusIn,
  input  PC_E,
  input  Clock,
  input  Clear,
  output [15:0] AddrBusOut
);

  wire [15:0] adder_1_out, multiplexer_1_out;

  Register #(.width(16)) register_1 (.D(multiplexer_1_out), .en(PC_E), .clk(Clock), .Q(AddrBusOut), .clr(Clear));
  Multiplexer #(.width(16)) multiplexer_1 (.in0(adder_1_out), .in1(AddrBusIn), .out(multiplexer_1_out), .sel(load));
  Adder #(.width(16)) adder_1 (.a(AddrBusOut), .b(16'h1), .out(adder_1_out), .cin(1'b0));  // open: cout
endmodule

module flagReg (
  input  [7:0] Din,
  input  Carryin,
  input  WE,
  input  Clck,
  input  Rst,
  output [3:0] Dout,
  output Cout
);

  wire [3:3] and_1_out;

  and and_1 (and_1_out[3], ~Din[0], ~Din[1], ~Din[2], ~Din[3], ~Din[4], ~Din[5], ~Din[6], ~Din[7]);  // AND_Gate
  Register #(.width(4)) register_1 (
    .D({and_1_out[3], Din[0], Din[7], Carryin}), .en(WE), .clk(Clck), .Q({Dout[3:1], Cout}), .clr(Rst));

  assign Dout[0] = Cout;

  // Notes on the sheet:
  //   odd
  //   N
  //   Z
endmodule

module CLK (
  input  butEnable,
  input  button,
  input  Halt,
  input  reset,
  output Rise,
  output Fall,
  output FullClock,
  output c2,
  output c1
);

  wire and_1_out, clock_1_out, not_1_out, not_2_out, not_3_out, not_4_out, not_5_out, or_1_out;

  Clock clock_1 (.out(clock_1_out));
  and and_1 (and_1_out, butEnable, button);
  or or_1 (or_1_out, and_1_out, clock_1_out);
  and and_2 (FullClock, or_1_out, ~Halt);  // AND_Gate
  not not_1 (not_1_out, FullClock);
  and and_3 (Rise, FullClock, not_1_out);
  not not_2 (not_2_out, FullClock);
  not not_3 (not_3_out, FullClock);
  and and_4 (Fall, not_2_out, not_4_out);
  not not_4 (not_4_out, not_3_out);
  not not_5 (not_5_out, FullClock);
  J_K_Flip_Flop j_k_ff_1 (.J(1'b1), .K(1'b1), .clk(not_5_out), .Q(c2), .reset(reset));  // open: Qn, preset
  J_K_Flip_Flop j_k_ff_2 (.J(1'b1), .K(1'b1), .clk(FullClock), .Q(c1), .reset(reset));  // open: Qn, preset
endmodule

module RegBank (
  input  [7:0] Datain,
  input  OE,
  input  Clk,
  input  reset,
  input  [2:0] SEL,
  input  WE,
  input  HL_OE,
  output Aoe,
  output Awe,
  output [7:0] DataOut,
  output [15:0] AddrBus
);

  wire decoder_1_out1, decoder_1_out2, decoder_1_out3, decoder_1_out4, decoder_1_out5, decoder_1_out6,
       decoder_1_out7, decoder_2_out1, decoder_2_out2, decoder_2_out3, decoder_2_out4, decoder_2_out5,
       decoder_2_out6, decoder_2_out7;
  wire [15:0] hlreg_1_dout;

  Decoder #(.select(3)) decoder_1 (
    .out0(Aoe), .out1(decoder_1_out1), .out2(decoder_1_out2), .out3(decoder_1_out3), .out4(decoder_1_out4),
    .out5(decoder_1_out5), .out6(decoder_1_out6), .out7(decoder_1_out7), .sel(SEL), .en(OE));
  Decoder #(.select(3)) decoder_2 (
    .out0(Awe), .out1(decoder_2_out1), .out2(decoder_2_out2), .out3(decoder_2_out3), .out4(decoder_2_out4),
    .out5(decoder_2_out5), .out6(decoder_2_out6), .out7(decoder_2_out7), .sel(SEL), .en(WE));
  regs B (
    .Din(Datain), .WE(decoder_2_out1), .Clck(Clk), .Rst(reset), .OE(decoder_1_out1), .Dout(DataOut));  // open: alwaysDOUT
  regs C (
    .Din(Datain), .WE(decoder_2_out2), .Clck(Clk), .Rst(reset), .OE(decoder_1_out2), .Dout(DataOut));  // open: alwaysDOUT
  regs D (
    .Din(Datain), .WE(decoder_2_out3), .Clck(Clk), .Rst(reset), .OE(decoder_1_out3), .Dout(DataOut));  // open: alwaysDOUT
  regs E (
    .Din(Datain), .WE(decoder_2_out4), .Clck(Clk), .Rst(reset), .OE(decoder_1_out4), .Dout(DataOut));  // open: alwaysDOUT
  regs S (
    .Din(Datain), .WE(decoder_2_out7), .Clck(Clk), .Rst(reset), .OE(decoder_1_out7), .Dout(DataOut));  // open: alwaysDOUT
  HLreg hlreg_1 (
    .reset(reset), .Din(Datain), .clock(Clk), .Hoe(decoder_1_out5), .Loe(decoder_1_out6),
    .Hwe(decoder_2_out6), .Lwe(decoder_2_out5), .H_out(DataOut), .Dout(hlreg_1_dout), .L_out(DataOut));
  assign AddrBus = HL_OE ? hlreg_1_dout : 16'bz;  // Controlled_Buffer controlled_buffer_1

  // Other names for the same wires on the sheet: rst = reset
endmodule

module HLreg (
  input  [7:0] Din,
  input  Hoe,
  input  Hwe,
  input  Lwe,
  input  Loe,
  input  clock,
  input  reset,
  output [7:0] H_out,
  output [15:0] Dout,
  output [7:0] L_out
);

  Register H (.D(Din), .en(Hwe), .clk(clock), .Q(Dout[15:8]), .clr(reset));
  Register L (.D(Din), .en(Lwe), .clk(clock), .Q(Dout[7:0]), .clr(reset));
  assign H_out = Hoe ? Dout[15:8] : 8'bz;  // Controlled_Buffer controlled_buffer_1
  assign L_out = Loe ? Dout[7:0] : 8'bz;  // Controlled_Buffer controlled_buffer_2
endmodule

module sequencer4step (
  input  resetState,
  input  clock,
  output out_3,
  output out_4,
  output out_5,
  output out_6
);

  wire d_ff_1_q, d_ff_1_qn, d_ff_2_q, d_ff_2_qn;

  D_Flip_Flop d_ff_1 (
    .D(d_ff_1_qn), .clk(clock), .Q(d_ff_1_q), .Qn(d_ff_1_qn), .preset(resetState), .reset(resetState));
  D_Flip_Flop d_ff_2 (
    .D(d_ff_2_qn), .clk(d_ff_1_q), .Q(d_ff_2_q), .Qn(d_ff_2_qn), .preset(resetState), .reset(resetState));
  and and_1 (out_4, d_ff_1_q, d_ff_2_q);
  and and_2 (out_5, d_ff_2_q, d_ff_1_qn);
  and and_3 (out_6, d_ff_1_q, d_ff_2_qn);
  and and_4 (out_3, d_ff_2_qn, d_ff_1_qn);
endmodule

module ALU2 (
  input  CEnbl,
  input  Cin,
  input  [7:0] A,
  input  [7:0] B,
  input  [2:0] OP,
  input  OutEn,
  output [7:0] out_7,
  output COut,
  output Z,
  output SaveFlag,
  output N,
  output V
);

  wire adder_1_cout, and_1_out, and_3_out, decoder_1_out0, decoder_1_out2, decoder_1_out3, decoder_1_out4,
       decoder_1_out5, nor_1_out, not_2_out, or_1_out, xor_2_out, xor_4_out, xor_5_out;
  wire [7:0] adder_1_out, and_2_out, controlled_buffer_1_out, not_1_out, or_2_out, xor_1_out, xor_3_out;
  wire [7:7] decoder_1_out1;

  // Probe on A
  // Probe on B
  assign xor_1_out = B ^ {8{decoder_1_out1[7]}};  // XOR_Gate xor_1, 8 bits wide
  Decoder #(.select(3)) decoder_1 (
    .out0(decoder_1_out0), .out1(decoder_1_out1[7]), .out2(decoder_1_out2), .out3(decoder_1_out3),
    .out4(decoder_1_out4), .out5(decoder_1_out5), .sel(OP), .en(1'b1));  // open: out6, out7
  and and_1 (and_1_out, CEnbl, Cin);
  xor xor_2 (xor_2_out, and_1_out, decoder_1_out1[7]);
  or or_1 (or_1_out, decoder_1_out1[7], decoder_1_out0);
  assign controlled_buffer_1_out = or_1_out ? adder_1_out : 8'bz;  // Controlled_Buffer controlled_buffer_1
  Adder adder_1 (.a(A), .b(xor_1_out), .out(adder_1_out), .cin(xor_2_out), .cout(adder_1_cout));
  assign and_2_out = A & xor_1_out;  // AND_Gate and_2, 8 bits wide
  assign controlled_buffer_1_out = decoder_1_out2 ? and_2_out : 8'bz;  // Controlled_Buffer controlled_buffer_2
  assign or_2_out = A | xor_1_out;  // OR_Gate or_2, 8 bits wide
  assign controlled_buffer_1_out = decoder_1_out3 ? or_2_out : 8'bz;  // Controlled_Buffer controlled_buffer_3
  assign xor_3_out = A ^ xor_1_out;  // XOR_Gate xor_3, 8 bits wide
  assign controlled_buffer_1_out = decoder_1_out4 ? xor_3_out : 8'bz;  // Controlled_Buffer controlled_buffer_4
  assign not_1_out = ~xor_1_out;  // NOT_Gate not_1, 8 bits wide
  assign controlled_buffer_1_out = decoder_1_out5 ? not_1_out : 8'bz;  // Controlled_Buffer controlled_buffer_5
  xor xor_4 (xor_4_out, controlled_buffer_1_out[7], A[7]);
  xor xor_5 (xor_5_out, A[7], B[7]);
  not not_2 (not_2_out, xor_5_out);
  nor nor_1 (nor_1_out, controlled_buffer_1_out[0], controlled_buffer_1_out[1], controlled_buffer_1_out[2], controlled_buffer_1_out[3], controlled_buffer_1_out[4], controlled_buffer_1_out[5], controlled_buffer_1_out[6], controlled_buffer_1_out[7]);
  and and_3 (and_3_out, xor_4_out, not_2_out);
  assign out_7 = OutEn ? controlled_buffer_1_out : 8'bz;  // Controlled_Buffer controlled_buffer_6
  assign COut = OutEn ? adder_1_cout : 1'bz;  // Controlled_Buffer controlled_buffer_7
  assign Z = OutEn ? nor_1_out : 1'bz;  // Controlled_Buffer controlled_buffer_8
  assign N = OutEn ? controlled_buffer_1_out[7] : 1'bz;  // Controlled_Buffer controlled_buffer_9
  assign V = OutEn ? and_3_out : 1'bz;  // Controlled_Buffer controlled_buffer_10
  // Probe on out_7

  assign SaveFlag = OutEn;
endmodule

module testt (
  input  in_1,
  input  in_2,
  input  in_3,
  output [7:0] out_4
);

  wire addrdecoder_1_p1, addrdecoder_1_p2, addrdecoder_1_p3, addrdecoder_2_p1, alu_1_cout, ALU_EN, and_2_out,
       Aoe, Awe, clck, clk, control_1_p8, control_1_p19, control_1_p20, control_1_p21, Fi2,
       FLAG_REGISTER_cout, HL_OE, instrdecoder_1_aluop, instrdecoder_1_cmp_op, instrdecoder_1_hlt,
       instrdecoder_1_hluse, instrdecoder_1_immreg, instrdecoder_1_jnz, instrdecoder_1_jz,
       instrdecoder_1_lda, instrdecoder_1_lw, instrdecoder_1_mov, instrdecoder_1_sw, IREG_WE, j_k_ff_1_q,
       j_k_ff_2_q, MEM_OE, MEM_WE, not_1_out, not_2_out, REG_OE, REG_WE, rst, sequencer4step_1_out_3,
       sequencer4step_1_out_4, sequencer4step_1_out_5, sequencer4step_1_out_6, TEMP_OE, TEMP_WE, undriven,
       undriven_2;
  wire [2:0] RegMux, RegMuxID;
  wire [3:0] Flag;
  wire [5:0] instrdecoder_1_add_op;
  wire [7:0] ACCUMULATOR_dout, alu_1_dout, instrreg_1_out_5, rom_1_data, rom_2_data, TEMP_dout;
  wire [14:0] addrdecoder_1_p4, addrdecoder_2_p2;
  wire [15:0] pc_1_addrbusout, pc_2_addrbusout, regbank_1_p11;

  regs ACCUMULATOR (
    .Din(alu_1_dout), .WE(Awe), .Clck(clk), .Rst(rst), .OE(Aoe), .Dout(ACCUMULATOR_dout));  // open: alwaysDOUT
  J_K_Flip_Flop j_k_ff_1 (.J(1'b1), .K(1'b1), .clk(not_1_out), .Q(j_k_ff_1_q), .reset(rst));  // open: Qn, preset
  not not_1 (not_1_out, clk);
  J_K_Flip_Flop j_k_ff_2 (.J(1'b1), .K(1'b1), .clk(clk), .Q(j_k_ff_2_q), .reset(rst));  // open: Qn, preset
  PC pc_1 (.AddrBusOut(pc_1_addrbusout));  // open: load, AddrBusIn, PC_E, Clock, Clear
  HLreg hlreg_1 (.clock(clck), .Dout(pc_1_addrbusout));  // open: reset, Din, Hoe, Loe, Hwe, Lwe, H_out, L_out
  regs TEMP (
    .Din(alu_1_dout), .WE(TEMP_WE), .Clck(clk), .Rst(rst), .OE(TEMP_OE), .Dout(TEMP_dout));  // open: alwaysDOUT
  not not_2 (not_2_out, instrdecoder_1_hlt);
  // Probe on undriven
  and and_1 (Fi2, not_2_out, j_k_ff_1_q);
  and and_2 (and_2_out, not_2_out, j_k_ff_2_q);
  // addrDecoder addrdecoder_1: pin names not known; wires that end beside it: addrdecoder_1_p1, addrdecoder_1_p2, addrdecoder_1_p3, addrdecoder_1_p4
  flagReg FLAG_REGISTER (
    .Din(alu_1_dout), .Carryin(alu_1_cout), .WE(undriven_2), .Clck(clk), .Rst(rst), .Dout(Flag),
    .Cout(FLAG_REGISTER_cout));
  ALU alu_1 (
    .A(ACCUMULATOR_dout), .B(TEMP_dout), .in_6(instrdecoder_1_add_op), .Cin(FLAG_REGISTER_cout),
    .OutEn({ALU_EN, undriven_2}), .Dout(alu_1_dout), .COut(alu_1_cout));  // open: CEnbl
  sequencer4step sequencer4step_1 (
    .resetState(rst), .clock(and_2_out), .out_3(sequencer4step_1_out_3), .out_4(sequencer4step_1_out_4),
    .out_5(sequencer4step_1_out_5), .out_6(sequencer4step_1_out_6));
  ROM #(.addrWidth(15)) rom_1 (.addr(addrdecoder_1_p4), .data(rom_1_data));
  RAM #(.addrWidth(15), .databus("bidir")) ram_1 (
    .addr(addrdecoder_1_p4), .we(addrdecoder_1_p1), .oe(addrdecoder_1_p2), .clk(clck), .data(out_4));
  assign out_4 = addrdecoder_1_p3 ? rom_1_data : 8'bz;  // Controlled_Buffer controlled_buffer_1
  instrReg instrreg_1 (.WE(IREG_WE), .instIn(alu_1_dout), .Clck(clk), .Rst(rst), .out_5(instrreg_1_out_5));
  instrDecoder instrdecoder_1 (
    .instr(instrreg_1_out_5), .HLT(instrdecoder_1_hlt), .ALUop(instrdecoder_1_aluop), .REG_MUX(RegMuxID),
    .immReg(instrdecoder_1_immreg), .LW(instrdecoder_1_lw), .SW(instrdecoder_1_sw), .MOV(instrdecoder_1_mov),
    .AND_op(instrdecoder_1_add_op[2]), .OR_op(instrdecoder_1_add_op[3]), .XOR_op(instrdecoder_1_add_op[4]),
    .NOT_op(instrdecoder_1_add_op[5]), .LDA(instrdecoder_1_lda), .JNZ(instrdecoder_1_jnz),
    .JZ(instrdecoder_1_jz), .ADD_op(instrdecoder_1_add_op[0]), .CMP_op(instrdecoder_1_cmp_op),
    .SUB_op(instrdecoder_1_add_op[1]), .HLuse(instrdecoder_1_hluse));  // open: NOP, JMP
  // Control control_1: pin names not known; wires that end beside it: and_2_out, sequencer4step_1_out_3, sequencer4step_1_out_4, sequencer4step_1_out_5, sequencer4step_1_out_6, RegMuxID, Flag, control_1_p8, instrdecoder_1_lw, instrdecoder_1_sw, instrdecoder_1_mov, instrdecoder_1_lda, instrdecoder_1_jnz, instrdecoder_1_jz, instrdecoder_1_hluse, instrdecoder_1_immreg, instrdecoder_1_aluop, instrdecoder_1_cmp_op, control_1_p19, control_1_p20, control_1_p21, IREG_WE, MEM_OE, REG_OE, TEMP_WE, TEMP_OE, MEM_WE, REG_WE, ALU_EN, RegMux, HL_OE
  // Probe on alu_1_dout
  Clock clock_1 (.out(clk));
  Button button_1 (.out(rst));
  PC pc_2 (
    .load(control_1_p19), .AddrBusIn(regbank_1_p11), .PC_E(control_1_p20), .Clock(clk), .Clear(rst),
    .AddrBusOut(pc_2_addrbusout));
  // Probe on pc_2_addrbusout
  // RegBank regbank_1: pin names not known; wires that end beside it: clk, rst, RegMux, HL_OE, REG_OE, REG_WE, Aoe, Awe, alu_1_dout, alu_1_dout, regbank_1_p11
  // addrDecoder addrdecoder_2: pin names not known; wires that end beside it: addrdecoder_2_p1, addrdecoder_2_p2
  ROM #(.addrWidth(15)) rom_2 (.addr(addrdecoder_2_p2), .data(rom_2_data));
  assign alu_1_dout = addrdecoder_2_p1 ? rom_2_data : 8'bz;  // Controlled_Buffer controlled_buffer_2

  // Notes on the sheet:
  //   contents of rom_1 (hex, n*v repeats v):
  //   1 2 3 4 5 6 7 8 9 a b c d e f 10 11 12
  //   contents of rom_2 (hex, n*v repeats v):
  //   0 4 ff ff 5 7*aa
endmodule

module addrDecoder (
  input  RAMwrite,
  input  MEMread,
  input  [15:0] PC,
  input  [15:0] HL,
  input  [15:0] imm,
  input  eHL,
  input  eIMM,
  output RAMwe,
  output RAMoe,
  output eROM,
  output [14:0] addrOut
);

  wire nor_1_out;
  wire [15:15] controlled_buffer_1_out;

  assign {controlled_buffer_1_out[15], addrOut} = nor_1_out ? PC : 16'bz;  // Controlled_Buffer controlled_buffer_1
  assign {controlled_buffer_1_out[15], addrOut} = eHL ? HL : 16'bz;  // Controlled_Buffer controlled_buffer_2
  nor nor_1 (nor_1_out, eHL, eIMM);
  Pull_Resistor pull_resistor_1 (.node({controlled_buffer_1_out[15], addrOut}));
  assign {controlled_buffer_1_out[15], addrOut} = eIMM ? imm : 16'bz;  // Controlled_Buffer controlled_buffer_3
  and and_1 (RAMwe, RAMwrite, controlled_buffer_1_out[15]);
  and and_2 (RAMoe, MEMread, controlled_buffer_1_out[15]);
  and and_3 (eROM, MEMread, ~controlled_buffer_1_out[15]);  // AND_Gate
  // Probe on addrOut

  // Notes on the sheet:
  //   0=ROM 1=RAM
endmodule

module Control (
  input  HL_use,
  input  NOP,
  input  c1,
  input  FETCH,
  input  EXC_1,
  input  EXC_2,
  input  LDA,
  input  CMPop,
  input  [2:0] REG_MUX,
  input  ALUop,
  input  LW,
  input  immReg,
  input  MOV,
  input  SW,
  input  EXC_3,
  input  JMP,
  input  JZ,
  input  JNZ,
  input  [3:0] FLAG,
  output HL_OE,
  output LOAD_ADDR,
  output PC_WE,
  output IReg_WE,
  output MEM_OE,
  output Reg_WE,
  output ALU_en,
  output [2:0] REGMUX,
  output Reg_OE,
  output Temp_WE,
  output Temp_OE,
  output HimmWE,
  output LimmWE,
  output immREGoe,
  output MEM_WE,
  output HLaddruse
);

  wire and_1_out, and_3_out, and_4_out, and_5_out, and_6_out, and_8_out, and_9_out, and_10_out, and_16_out,
       and_20_out, and_21_out, and_22_out, and_25_out, and_26_out, and_27_out, and_28_out, and_29_out,
       and_30_out, and_31_out, and_32_out, and_33_out, and_34_out, and_35_out, and_36_out, imm, immALUfetch,
       immALUpcinc, JMPimmLoad, JMPimmLoadpc, JMPpcInc, JMPpcLoadAddr, LDAexec1, LDAexec2, LWniWE, not_1_out,
       not_2_out, or_1_out, or_2_out, PCwe, SWniWE, SWoe, SWpcinc, SWwe, uncondJMP, xor_1_out;
  wire [2:2] and_23_out;

  and and_1 (and_1_out, ~c1, FETCH);  // AND_Gate
  not not_1 (not_1_out, c1);
  not not_2 (not_2_out, not_1_out);
  and and_2 (IReg_WE, c1, FETCH);
  and and_3 (and_3_out, ALUop, immReg);
  and and_4 (and_4_out, ALUop, ~immReg);  // AND_Gate
  and and_5 (and_5_out, not_2_out, EXC_1, SW, ~immReg);  // AND_Gate
  and and_6 (and_6_out, not_2_out, EXC_2, SW, ~immReg);  // AND_Gate
  and and_7 (SWwe, not_2_out, EXC_3, SW, ~immReg);  // AND_Gate
  and and_8 (and_8_out, SW, EXC_1, ~not_2_out, ~immReg);  // AND_Gate
  and and_9 (and_9_out, SW, EXC_2, ~not_2_out, ~immReg);  // AND_Gate
  and and_10 (and_10_out, ~not_2_out, EXC_1, immReg, JMP);  // AND_Gate
  and and_11 (uncondJMP, ~not_2_out, EXC_3, ~immReg, JMP);  // AND_Gate
  or or_1 (or_1_out, JZ, JMP, JNZ);
  and and_12 (LWniWE, LW, EXC_1, not_2_out, immReg);
  and and_13 (SWniWE, SW, EXC_1, not_2_out, immReg);
  and and_14 (LDAexec1, not_2_out, LDA, EXC_1);
  and and_15 (LDAexec2, not_2_out, LDA, EXC_2);
  assign REGMUX = or_2_out ? REG_MUX : 3'bz;  // Controlled_Buffer controlled_buffer_1
  or or_2 (or_2_out, SWniWE, SWwe, and_16_out, Temp_OE, and_35_out, LWniWE);
  and and_16 (and_16_out, EXC_1, not_2_out, and_3_out);
  and and_17 (ALU_en, ALUop, not_2_out, EXC_2);
  and and_18 (immALUfetch, EXC_1, not_2_out, and_4_out);
  and and_19 (immALUpcinc, and_4_out, ~not_2_out, EXC_1);  // AND_Gate
  and and_20 (and_20_out, EXC_2, ~not_2_out, ~immReg, LW);  // AND_Gate
  and and_21 (and_21_out, LW, not_2_out, EXC_1);
  and and_22 (and_22_out, LW, not_2_out, EXC_2);
  and and_23 (and_23_out[2], ~immReg, MOV, not_2_out, EXC_1);  // AND_Gate
  and and_24 (Temp_OE, ~immReg, MOV, not_2_out, EXC_2);  // AND_Gate
  or or_3 (SWpcinc, and_8_out, and_9_out);
  and and_25 (and_25_out, ~not_2_out, EXC_1, immReg, FLAG[3], JZ);  // AND_Gate
  and and_26 (and_26_out, ~not_2_out, EXC_1, immReg, ~FLAG[3], JNZ);  // AND_Gate
  and and_27 (and_27_out, ~not_2_out, EXC_3, ~immReg, FLAG[3], JZ);  // AND_Gate
  and and_28 (and_28_out, ~not_2_out, EXC_3, ~immReg, ~FLAG[3], JNZ);  // AND_Gate
  assign REGMUX = LDAexec2 ? {LDAexec2, 1'b0, LDAexec2} : 3'bz;  // Controlled_Buffer controlled_buffer_2
  or or_4 (JMPpcLoadAddr, and_25_out, and_10_out, and_26_out);
  and and_29 (and_29_out, or_1_out, not_2_out, EXC_1, ~immReg);  // AND_Gate
  and and_30 (and_30_out, or_1_out, not_2_out, EXC_2, ~immReg);  // AND_Gate
  and and_31 (and_31_out, or_1_out, EXC_1, ~not_2_out, ~immReg);  // AND_Gate
  and and_32 (and_32_out, or_1_out, EXC_2, ~not_2_out, ~immReg);  // AND_Gate
  or or_5 (JMPimmLoadpc, and_27_out, uncondJMP, and_28_out);
  xor xor_1 (xor_1_out, EXC_1, EXC_2);
  and and_33 (and_33_out, xor_1_out, ~c1, LDA);  // AND_Gate
  assign REGMUX = LDAexec1 ? {{2{LDAexec1}}, 1'b0} : 3'bz;  // Controlled_Buffer controlled_buffer_3
  not not_3 (imm, immReg);
  or or_6 (JMPimmLoad, and_29_out, and_30_out);
  or or_7 (JMPpcInc, and_31_out, and_32_out);
  and and_34 (and_34_out, and_21_out, ~immReg);  // AND_Gate
  and and_35 (and_35_out, and_22_out, ~immReg);  // AND_Gate
  or or_8 (LOAD_ADDR, JMPpcLoadAddr, JMPimmLoadpc);
  or or_9 (PCwe, and_20_out, and_34_out);
  or or_10 (HLaddruse, LWniWE, SWniWE);
  and and_36 (and_36_out, ALU_en, ~CMPop);  // AND_Gate
  assign REGMUX = ALU_en ? ~{3{ALU_en}} : 3'bz;  // Controlled_Inverter controlled_inverter_1
  assign REGMUX = and_23_out[2] ? ~{3{and_23_out[2]}} : 3'bz;  // Controlled_Inverter controlled_inverter_2
  or or_11 (SWoe, and_5_out, and_6_out);
  or or_12 (Reg_OE, and_16_out, and_23_out[2], SWwe, SWniWE);
  or or_13 (MEM_OE, JMPimmLoad, IReg_WE, LDAexec1, LDAexec2, SWoe, and_35_out, immALUfetch, LWniWE);
  or or_14 (Reg_WE, LDAexec1, LDAexec2, Temp_OE, and_35_out, and_36_out, LWniWE);
  or or_15 (Temp_WE, and_16_out, and_23_out[2], immALUfetch);
  or or_16 (HimmWE, and_29_out, and_5_out);
  or or_17 (LimmWE, and_30_out, and_6_out);
  or or_18 (immREGoe, SWwe, JMPimmLoadpc);
  or or_19 (MEM_WE, SWwe, SWniWE);
  or or_20 (PC_WE, immALUpcinc, and_33_out, and_1_out, SWpcinc, LOAD_ADDR, PCwe, JMPpcInc);

  assign HL_OE = HL_use;

  // Other names for the same wires on the sheet: clock = c1; exec1 = EXC_1; exec2 = EXC_2; Zflag = FLAG[3];
  //   LWnotimm = LW; SWnotimm = SW

  // Notes on the sheet:
  //   e3
  //   imm
  //   e2
  //   e1
  //   C
  //   На 3 цикл запиши данные по аддресу
  //   первый цикл прочти первые 8 бит адресса, на второй прочти следующие 8
endmodule

module Key_board (
  input  in_1
);

  wire button_1_out, clock_1_out, keyboard_1_avail;
  wire [6:0] keyboard_1_data;
  wire [7:7] pull_resistor_1_node;

  Clock clock_1 (.out(clock_1_out));
  Keyboard keyboard_1 (
    .clk(clock_1_out), .re(in_1), .clr(button_1_out), .avail(keyboard_1_avail), .data(keyboard_1_data));
  Pull_Resistor pull_resistor_1 (.node(pull_resistor_1_node[7]));
  Register register_1 (
    .D({pull_resistor_1_node[7], keyboard_1_data}), .en(keyboard_1_avail), .clk(clock_1_out),
    .clr(button_1_out));  // open: Q
  Button button_1 (.out(button_1_out));
endmodule

module imm_addr_reg (
  input  [7:0] Din,
  input  Hwe,
  input  Lwe,
  input  clock,
  input  reset,
  output [15:0] Dout
);

  Register H (.D(Din), .en(Hwe), .clk(clock), .Q(Dout[15:8]), .clr(reset));
  Register L (.D(Din), .en(Lwe), .clk(clock), .Q(Dout[7:0]), .clr(reset));
endmodule

module CPU (
);

  wire addr_decoder_erom, addr_decoder_ramoe, addr_decoder_ramwe, ALU_chip_cout, ALU_EN, Aoe, Awe, c,
       Controller_himmwe, Controller_hladdruse, Controller_immregoe, Controller_limmwe, Controller_load_addr,
       Controller_pc_we, Decoder_aluop, Decoder_cmp_op, Decoder_hlt, Decoder_hluse, Decoder_immreg,
       Decoder_jmp, Decoder_jnz, Decoder_jz, Decoder_lda, Decoder_lw, Decoder_mov, Decoder_nop, Decoder_sw,
       Fi1, Fi2, FLAG_REGISTER_cout, HL_OE, IREG_WE, j_k_ff_1_q, j_k_ff_2_q, MEM_OE, MEM_WE, not_1_out,
       not_2_out, pull_resistor_1_node, REG_OE, REG_WE, rst, sequencer_out_3, sequencer_out_4,
       sequencer_out_5, sequencer_out_6, TEMP_OE, TEMP_WE, undriven;
  wire [2:0] RegMux, RegMuxID;
  wire [3:0] Flag;
  wire [5:0] Decoder_add_op;
  wire [7:0] ACCUMULATOR_alwaysdout, ACCUMULATOR_dout, Instr_reg_out_5, rom_1_data, TEMP_alwaysdout;
  wire [14:0] addr_decoder_addrout;
  wire [15:0] HLaddr, IMMaddr, multiplexer_1_out, Prg_counter_addrbusout;

  regs ACCUMULATOR (
    .Din(ACCUMULATOR_dout), .WE(Awe), .Clck(Fi2), .Rst(rst), .OE(Aoe), .Dout(ACCUMULATOR_dout),
    .alwaysDOUT(ACCUMULATOR_alwaysdout));
  not not_1 (not_1_out, c);
  Clock clock_1 (.out(c));
  Button button_1 (.out(rst));
  regs TEMP (
    .Din(ACCUMULATOR_dout), .WE(TEMP_WE), .Clck(Fi2), .Rst(rst), .OE(TEMP_OE), .Dout(ACCUMULATOR_dout),
    .alwaysDOUT(TEMP_alwaysdout));
  J_K_Flip_Flop j_k_ff_1 (.J(1'b1), .K(1'b1), .clk(not_1_out), .Q(j_k_ff_1_q), .reset(rst));  // open: Qn, preset
  J_K_Flip_Flop j_k_ff_2 (.J(1'b1), .K(1'b1), .clk(c), .Q(j_k_ff_2_q), .reset(rst));  // open: Qn, preset
  not not_2 (not_2_out, Decoder_hlt);
  and and_1 (Fi2, not_2_out, j_k_ff_1_q);
  and and_2 (Fi1, not_2_out, j_k_ff_2_q);
  flagReg FLAG_REGISTER (
    .Din(ACCUMULATOR_dout), .Carryin(ALU_chip_cout), .WE(undriven), .Clck(Fi2), .Rst(rst), .Dout(Flag),
    .Cout(FLAG_REGISTER_cout));
  ALU ALU_chip (
    .A(ACCUMULATOR_alwaysdout), .B(TEMP_alwaysdout), .in_6(Decoder_add_op), .Cin(FLAG_REGISTER_cout),
    .OutEn({ALU_EN, undriven}), .Dout(ACCUMULATOR_dout), .COut(ALU_chip_cout));  // open: CEnbl
  sequencer4step sequencer (
    .resetState(rst), .clock(Fi1), .out_3(sequencer_out_3), .out_4(sequencer_out_4), .out_5(sequencer_out_5),
    .out_6(sequencer_out_6));
  instrReg Instr_reg (.WE(IREG_WE), .instIn(ACCUMULATOR_dout), .Clck(Fi2), .Rst(rst), .out_5(Instr_reg_out_5));
  instrDecoder Decoder (
    .instr(Instr_reg_out_5), .HLT(Decoder_hlt), .ALUop(Decoder_aluop), .REG_MUX(RegMuxID),
    .immReg(Decoder_immreg), .NOP(Decoder_nop), .LW(Decoder_lw), .SW(Decoder_sw), .MOV(Decoder_mov),
    .AND_op(Decoder_add_op[2]), .OR_op(Decoder_add_op[3]), .XOR_op(Decoder_add_op[4]),
    .NOT_op(Decoder_add_op[5]), .LDA(Decoder_lda), .JNZ(Decoder_jnz), .JZ(Decoder_jz), .JMP(Decoder_jmp),
    .ADD_op(Decoder_add_op[0]), .CMP_op(Decoder_cmp_op), .SUB_op(Decoder_add_op[1]), .HLuse(Decoder_hluse));
  Control Controller (
    .JMP(Decoder_jmp), .JZ(Decoder_jz), .JNZ(Decoder_jnz), .LW(Decoder_lw), .SW(Decoder_sw),
    .ALUop(Decoder_aluop), .REG_MUX(RegMuxID), .NOP(Decoder_nop), .c1(Fi1), .FETCH(sequencer_out_3),
    .EXC_1(sequencer_out_4), .EXC_2(sequencer_out_5), .LDA(Decoder_lda), .MOV(Decoder_mov),
    .HL_use(Decoder_hluse), .CMPop(Decoder_cmp_op), .FLAG(Flag), .immReg(Decoder_immreg),
    .EXC_3(sequencer_out_6), .HLaddruse(Controller_hladdruse), .HL_OE(HL_OE),
    .LOAD_ADDR(Controller_load_addr), .IReg_WE(IREG_WE), .ALU_en(ALU_EN), .Temp_OE(TEMP_OE), .REGMUX(RegMux),
    .Reg_OE(REG_OE), .Temp_WE(TEMP_WE), .HimmWE(Controller_himmwe), .LimmWE(Controller_limmwe),
    .MEM_OE(MEM_OE), .Reg_WE(REG_WE), .immREGoe(Controller_immregoe), .MEM_WE(MEM_WE),
    .PC_WE(Controller_pc_we));
  // Probe on ACCUMULATOR_dout
  PC Prg_counter (
    .load(Controller_load_addr), .AddrBusIn(multiplexer_1_out), .PC_E(Controller_pc_we), .Clock(Fi1),
    .Clear(rst), .AddrBusOut(Prg_counter_addrbusout));
  Clock clock_2 ();  // open: out
  RegBank reg_bank (
    .OE(REG_OE), .Clk(Fi2), .reset(rst), .WE(REG_WE), .HL_OE(HL_OE), .SEL(RegMux), .Datain(ACCUMULATOR_dout),
    .Aoe(Aoe), .Awe(Awe), .DataOut(ACCUMULATOR_dout), .AddrBus(HLaddr));
  Multiplexer #(.width(16)) multiplexer_1 (
    .in0(HLaddr), .in1(IMMaddr), .out(multiplexer_1_out), .sel(Controller_immregoe));
  imm_addr_reg immReg (
    .reset(rst), .Din(ACCUMULATOR_dout), .clock(Fi2), .Hwe(Controller_himmwe), .Lwe(Controller_limmwe),
    .Dout(IMMaddr));
  addrDecoder addr_decoder (
    .eIMM(Controller_immregoe), .RAMwrite(MEM_WE), .MEMread(MEM_OE), .PC(Prg_counter_addrbusout),
    .HL(HLaddr), .imm(IMMaddr), .eHL(Controller_hladdruse), .RAMwe(addr_decoder_ramwe),
    .RAMoe(addr_decoder_ramoe), .eROM(addr_decoder_erom), .addrOut(addr_decoder_addrout));
  Pull_Resistor pull_resistor_1 (.node(pull_resistor_1_node));
  assign pull_resistor_1_node = Fi2 ? addr_decoder_ramwe : 1'bz;  // Controlled_Buffer controlled_buffer_1
  ROM #(.addrWidth(15)) rom_1 (.addr(addr_decoder_addrout), .data(rom_1_data));
  RAM #(.addrWidth(15), .clearpin("true"), .databus("bidir"), .trigger("high")) ram_1 (
    .addr(addr_decoder_addrout), .we(pull_resistor_1_node), .oe(addr_decoder_ramoe), .data(ACCUMULATOR_dout),
    .clr(rst));
  assign ACCUMULATOR_dout = addr_decoder_erom ? rom_1_data : 8'bz;  // Controlled_Buffer controlled_buffer_2

  // Notes on the sheet:
  //   CLOCK_GENERATOR
  //   C   Fi1 Fi2
  //   0  -  0   0
  //   1  -  1   0
  //   0  -  1   1
  //   1  -  0   1
  //   0  -  0   0
  //   if not HLT clocks are generated
  //   DATA_BUS
  //   DATA_BUS
  //   contents of rom_1 (hex, n*v repeats v):
  //   0 4 0 c 15 7*0 4 80 0 1 ff 12 4 80 6 11 ff
  //   DATA_BUS
endmodule
